# Fritzing sketch sensor-node.arduinopromini+nrf24.button-interrupt (saved by Fritzing 0.9.5d)
circuit board: 5.35384cm x 5.38549cm

parts:
  Arduino = Arduino Pro Mini (5V)
  U1 = LM3480IM4 [package=sot23-3]
  RF24 = NRF24L01+ Breakout Board
  S1 = Pushbutton [package=THT]
  S2 = Pushbutton [package=THT]
  S3 = Pushbutton [package=THT]
  D1 = Diode [package=diode-1n4001]
  D2 = Diode [package=diode-1n4001]
  D3 = Diode [package=diode-1n4001]
  R1 = Resistor [tolerance=±5% resistance=10k package=THT]
  C3 = Ceramic Capacitor [capacitance=100nF package="100 mil [THT, multilayer]"]
  C2 = Ceramic Capacitor [capacitance=100nF package="100 mil [THT, multilayer]"]
  C1 = Ceramic Capacitor [capacitance=100nF package="100 mil [THT, multilayer]"]

nets:
  5V: Arduino.VCC, U1.IN, R1.Pin_1
  GND: Arduino.GND, U1.GND, RF24.GND, S1.leg0, S2.leg0, S3.leg0, C3.0, C2.0, C1.0
  N1: Arduino.SCK, RF24.SCK
  N2: Arduino.MISO, RF24.MISO
  N3: Arduino.MOSI, RF24.MOSI
  N4: Arduino.D10, RF24.CS
  N5: Arduino.D9, RF24.CE
  N6: Arduino.D5, S2.leg1, D2.C, C2.1
  N7: Arduino.D4, S1.leg1, D1.C, C1.1
  N8: Arduino.D3, D1.A, D2.A, D3.A, R1.Pin_0
  N9: Arduino.D2, RF24.IRQ
  3.3V: U1.OUT, RF24.VCC
  N10: S3.leg1, D3.C, C3.1

notes:
  C1,2,3 to debounce
